// Digital circuit ALU.dig as structural Verilog
module ALU (
  input  [7:0] D_IN,
  input  A_LD,
  input  nA_LD,
  input  A_OE,
  input  A_SEL,
  input  ALU_S0,
  input  ALU_S1,
  input  ALU_S2,
  input  ALU_CIN,
  input  nSHR_OE,
  input  SHR_IN0,
  input  CLK,
  input  RST,
  output [7:0] D_OUT,
  output Z_FLAG,
  output N_FLAG,
  output C_FLAG,
  output V_FLAG
);

  wire _7402_1_pin1, _7402_1_pin4, _7402_1_pin10, _7402_1_pin13, _74173_1_pin3, _74173_1_pin4, _74173_1_pin5,
       _74173_1_pin6, _74173_2_pin3, _74173_2_pin4, _74173_2_pin5, _74173_2_pin6, _74257_1_pin3,
       _74257_1_pin4, _74257_1_pin6, _74257_1_pin7, _74257_1_pin9, _74257_1_pin10, _74257_1_pin12,
       _74257_1_pin13, _74257_2_pin3, _74257_2_pin4, _74257_2_pin6, _74257_2_pin7, _74257_2_pin9,
       _74257_2_pin10, _74257_2_pin12, _74382_1_pin14, A_LOAD, C_FLAG_t, V_FLAG_t;

  _7408 _7408_1 (
    .pin1(A_LD), .pin2(nA_LD), .pin3(A_LOAD), .pin4(1'b0), .pin5(1'b0), .pin7(1'b0), .pin9(1'b0),
    .pin10(1'b0), .pin12(1'b0), .pin13(1'b0), .pin14(1'b1));  // open: pin6, pin8, pin11
  _74257 _74257_1 (
    .pin1(A_SEL), .pin2(D_IN[0]), .pin3(_74257_1_pin3), .pin4(_74257_1_pin4), .pin5(D_IN[1]),
    .pin6(_74257_1_pin6), .pin7(_74257_1_pin7), .pin8(1'b0), .pin9(_74257_1_pin9), .pin10(_74257_1_pin10),
    .pin11(D_IN[2]), .pin12(_74257_1_pin12), .pin13(_74257_1_pin13), .pin14(D_IN[3]), .pin15(1'b0),
    .pin16(1'b1));
  _74173 _74173_1 (
    .pin1(1'b0), .pin2(1'b0), .pin3(_74173_1_pin3), .pin4(_74173_1_pin4), .pin5(_74173_1_pin5),
    .pin6(_74173_1_pin6), .pin7(CLK), .pin8(1'b0), .pin9(A_LOAD), .pin10(A_LOAD), .pin11(_74257_1_pin12),
    .pin12(_74257_1_pin9), .pin13(_74257_1_pin7), .pin14(_74257_1_pin4), .pin15(RST), .pin16(1'b1));
  _74382 _74382_1 (
    .pin1(_74173_1_pin4), .pin2(D_IN[1]), .pin3(_74173_1_pin3), .pin4(D_IN[0]), .pin5(ALU_S0), .pin6(ALU_S1),
    .pin7(ALU_S2), .pin8(_74257_1_pin3), .pin9(_74257_1_pin6), .pin10(1'b0), .pin11(_74257_1_pin10),
    .pin12(_74257_1_pin13), .pin14(_74382_1_pin14), .pin15(ALU_CIN), .pin16(D_IN[3]), .pin17(_74173_1_pin6),
    .pin18(D_IN[2]), .pin19(_74173_1_pin5), .pin20(1'b1));  // open: pin13
  _74257 _74257_2 (
    .pin1(A_SEL), .pin2(D_IN[4]), .pin3(_74257_2_pin3), .pin4(_74257_2_pin4), .pin5(D_IN[5]),
    .pin6(_74257_2_pin6), .pin7(_74257_2_pin7), .pin8(1'b0), .pin9(_74257_2_pin9), .pin10(_74257_2_pin10),
    .pin11(D_IN[6]), .pin12(_74257_2_pin12), .pin13(N_FLAG), .pin14(D_IN[7]), .pin15(1'b0), .pin16(1'b1));
  _74173 _74173_2 (
    .pin1(1'b0), .pin2(1'b0), .pin3(_74173_2_pin3), .pin4(_74173_2_pin4), .pin5(_74173_2_pin5),
    .pin6(_74173_2_pin6), .pin7(CLK), .pin8(1'b0), .pin9(A_LOAD), .pin10(A_LOAD), .pin11(_74257_2_pin12),
    .pin12(_74257_2_pin9), .pin13(_74257_2_pin7), .pin14(_74257_2_pin4), .pin15(RST), .pin16(1'b1));
  _74382 _74382_2 (
    .pin1(_74173_2_pin4), .pin2(D_IN[5]), .pin3(_74173_2_pin3), .pin4(D_IN[4]), .pin5(ALU_S0), .pin6(ALU_S1),
    .pin7(ALU_S2), .pin8(_74257_2_pin3), .pin9(_74257_2_pin6), .pin10(1'b0), .pin11(_74257_2_pin10),
    .pin12(N_FLAG), .pin13(V_FLAG_t), .pin14(C_FLAG_t), .pin15(_74382_1_pin14), .pin16(D_IN[7]),
    .pin17(_74173_2_pin6), .pin18(D_IN[6]), .pin19(_74173_2_pin5), .pin20(1'b1));
  _7402 _7402_1 (
    .pin1(_7402_1_pin1), .pin2(_74257_2_pin6), .pin3(_74257_2_pin3), .pin4(_7402_1_pin4),
    .pin5(_74257_1_pin3), .pin6(_74257_1_pin6), .pin7(1'b0), .pin8(_74257_1_pin10), .pin9(_74257_1_pin13),
    .pin10(_7402_1_pin10), .pin11(_74257_2_pin10), .pin12(N_FLAG), .pin13(_7402_1_pin13), .pin14(1'b1));
  _7421 _7421_1 (
    .pin1(_7402_1_pin10), .pin2(_7402_1_pin13), .pin4(_7402_1_pin1), .pin5(_7402_1_pin4), .pin6(Z_FLAG),
    .pin7(1'b0), .pin9(1'b0), .pin10(1'b0), .pin12(1'b0), .pin13(1'b0), .pin14(1'b1));  // open: pin3, pin8, pin11
  _74245 _74245_1 (
    .pin1(1'b1), .pin2(_74173_1_pin4), .pin3(_74173_1_pin5), .pin4(_74173_1_pin6), .pin5(_74173_2_pin3),
    .pin6(_74173_2_pin4), .pin7(_74173_2_pin5), .pin8(_74173_2_pin6), .pin9(SHR_IN0), .pin10(1'b0),
    .pin11(D_OUT[7]), .pin12(D_OUT[6]), .pin13(D_OUT[5]), .pin14(D_OUT[4]), .pin15(D_OUT[3]),
    .pin16(D_OUT[2]), .pin17(D_OUT[1]), .pin18(D_OUT[0]), .pin19(nSHR_OE), .pin20(1'b1));
  _74245 _74245_2 (
    .pin1(1'b1), .pin2(_74173_1_pin3), .pin3(_74173_1_pin4), .pin4(_74173_1_pin5), .pin5(_74173_1_pin6),
    .pin6(_74173_2_pin3), .pin7(_74173_2_pin4), .pin8(_74173_2_pin5), .pin9(_74173_2_pin6), .pin10(1'b0),
    .pin11(D_OUT[7]), .pin12(D_OUT[6]), .pin13(D_OUT[5]), .pin14(D_OUT[4]), .pin15(D_OUT[3]),
    .pin16(D_OUT[2]), .pin17(D_OUT[1]), .pin18(D_OUT[0]), .pin19(A_OE), .pin20(1'b1));
  _74157 _74157_1 (
    .pin1(nSHR_OE), .pin2(_74173_1_pin3), .pin3(C_FLAG_t), .pin4(C_FLAG), .pin5(1'b0), .pin6(V_FLAG_t),
    .pin7(V_FLAG), .pin8(1'b0), .pin10(1'b0), .pin11(1'b0), .pin13(1'b0), .pin14(1'b0), .pin15(1'b0),
    .pin16(1'b1));  // open: pin9, pin12

  // Other names for the same wires on the sheet: SHR = nSHR_OE; SHR_D7 = SHR_IN0
endmodule
