// Digital circuit CPU.dig as structural Verilog
module CPU (
  input  CLK,
  input  clk_2,
  input  CLK_SEL,
  output [7:0] opcode,
  output [15:0] rom
);

  wire A_LD, A_OE, A_SEL, addr_dec_1_p2, addr_dec_1_p3, alu_1_c_flag, alu_1_n_flag, alu_1_v_flag,
       alu_1_z_flag, ALU_CIN, ALU_S0, ALU_S1, ALU_S2, and_1_out, and_2_out, and_3_out, C, CLK_t, FL_SEL,
       keyboard_1_av, MAR_DIR, mmio_1_kb_en, N, nA_LD, nFL_OE, nFLCV_LD, nFLZN_LD, nHALT, nHBA_OE, nIRA_OE,
       nIRD_OE, nIRH_LD, nIRL_LD, nJ_LD, nJ_OE, nMAR_INC, nMAR_OE, nMARH_LD, nMARL_LD, nMEM_RD, nMEM_WR,
       nMMIO_CS, nMPC_RST, nPC_LD, nPCH_OE, nPCL_OE, nRST, nSHR_OE, nSP_INC, nSP_LD, nSP_OE, nSPH_OE,
       nSPL_OE, nXY_INC, nXYA_OE, PC_INC, PC_OE, REG_LD, REG_OE, reset_1_out, RST, RST_out, SHR_IN0, SP_DIR,
       SRC_SEL, V, XY_DIR, Z;
  wire [2:0] Rsrc;
  wire [3:0] max7219_sim_1_dig1, max7219_sim_1_dig2, max7219_sim_1_dig3, max7219_sim_1_dig4,
       max7219_sim_1_dig5, max7219_sim_1_dig6, max7219_sim_1_dig7, max7219_sim_1_dig8;
  wire [4:0] mmio_1_spi_out;
  wire [7:0] ir_1_ab, keyboard_1_d, mmio_1_display, pc_1_p11;
  wire [15:0] addr_buffer_1_a_bus;
  wire [15:8] keyboard_1_d_2;
  wire [15:13] ctrlunit_1_c32_47;
  wire [15:14] ctrlunit_1_c0_15;

  Button #(.activeLow("true")) u_RST (.out(RST_out));
  Reset reset_1 (.out(reset_1_out));
  and and_1 (and_1_out, RST_out, reset_1_out);
  and and_2 (and_2_out, CLK, ~CLK_SEL);  // And
  and and_3 (and_3_out, CLK_SEL, clk_2);
  RST_HARDWARE rst_hardware_1 (.CLK(CLK_t), .RST_IN(and_1_out), .RST(RST), .nRST(nRST));
  or or_1 (CLK_t, and_2_out, and_3_out);
  addr_buffer addr_buffer_1 (.AB_L(ir_1_ab), .nHBA_OE(nHBA_OE), .nRST(nRST), .A_BUS(addr_buffer_1_a_bus));
  Seven_Seg_Hex seven_seg_hex_1 (.d(max7219_sim_1_dig8), .dp(1'b0));
  Seven_Seg_Hex seven_seg_hex_2 (.d(max7219_sim_1_dig7), .dp(1'b0));
  // ADDR_DEC addr_dec_1: pin names not known; wires that end beside it: addr_buffer_1_a_bus, addr_dec_1_p2, addr_dec_1_p3, nMMIO_CS
  Seven_Seg_Hex seven_seg_hex_3 (.d(max7219_sim_1_dig6), .dp(1'b0));
  // NotConnected on addr_buffer_1_a_bus[7:0]
  // PC pc_1: pin names not known; wires that end beside it: addr_buffer_1_a_bus, PC_INC, nPC_LD, PC_OE, nPCL_OE, nPCH_OE, CLK_t, RST, nRST, addr_buffer_1_a_bus, pc_1_p11
  // SP sp_1: pin names not known; wires that end beside it: addr_buffer_1_a_bus, nSP_INC, SP_DIR, nSP_LD, nSP_OE, nSPH_OE, nSPL_OE, CLK_t
  Seven_Seg_Hex seven_seg_hex_4 (.d(max7219_sim_1_dig5), .dp(1'b0));
  J_REG j_reg_1 (.D_BUS(pc_1_p11), .nJ_LD(nJ_LD), .nJ_OE(nJ_OE), .CLK(CLK_t), .AH_BUS(addr_buffer_1_a_bus[15:8]));
  // MAR mar_1: pin names not known; wires that end beside it: addr_buffer_1_a_bus, CLK_t, MAR_DIR, nMAR_INC, nMAR_OE, nMARH_LD, nMARL_LD, pc_1_p11, addr_buffer_1_a_bus, pc_1_p11
  Seven_Seg_Hex seven_seg_hex_5 (.d(max7219_sim_1_dig4), .dp(1'b0));
  RAMSinglePortSel #(.AddrBits(16), .Bits(8)) ramsingleportsel_1 (
    .A(addr_buffer_1_a_bus), .CS(~addr_dec_1_p2), .WE(~nMEM_WR), .OE(~nMEM_RD), .D(pc_1_p11));
  EEPROM #(.AddrBits(15), .Bits(16)) eeprom_1 (
    .A({1'b0, addr_buffer_1_a_bus[13:0]}), .CS(~addr_dec_1_p3), .WE(1'b0), .OE(~nMEM_RD), .D(rom));
  Seven_Seg_Hex seven_seg_hex_6 (.d(max7219_sim_1_dig3), .dp(1'b0));
  Seven_Seg_Hex seven_seg_hex_7 (.d(max7219_sim_1_dig2), .dp(1'b0));
  RFILE rfile_1 (
    .DB_IN(pc_1_p11), .B_10_8(opcode[2:0]), .B_7_5(Rsrc), .REG_LD_EN(REG_LD), .REG_OE_EN(REG_OE),
    .nXY_INC(nXY_INC), .XY_DIR(XY_DIR), .nXYA_OE(nXYA_OE), .SRC_SEL(SRC_SEL), .CLK(CLK_t), .RST(RST),
    .DB_OUT(pc_1_p11), .AB_OUT(addr_buffer_1_a_bus), .A_LD(A_LD), .A_OE(A_OE));
  ALU alu_1 (
    .D_IN(pc_1_p11), .A_LD(A_LD), .nA_LD(nA_LD), .A_OE(A_OE), .A_SEL(A_SEL), .ALU_S0(ALU_S0),
    .ALU_S1(ALU_S1), .ALU_S2(ALU_S2), .ALU_CIN(ALU_CIN), .nSHR_OE(nSHR_OE), .SHR_IN0(SHR_IN0), .CLK(CLK_t),
    .RST(RST), .D_OUT(pc_1_p11), .Z_FLAG(alu_1_z_flag), .N_FLAG(alu_1_n_flag), .C_FLAG(alu_1_c_flag),
    .V_FLAG(alu_1_v_flag));
  IR ir_1 (
    .ROM_IN(rom), .nIRH_LD(nIRH_LD), .nIRL_LD(nIRL_LD), .nIRD_OE(nIRD_OE), .nIRA_OE(nIRA_OE), .CLK(CLK_t),
    ._15_11(opcode[7:3]), ._10_8(opcode[2:0]), ._7_5(Rsrc), ._0_7(pc_1_p11), .AB(ir_1_ab));
  Seven_Seg_Hex seven_seg_hex_8 (.d(max7219_sim_1_dig1), .dp(1'b0));
  MMIO mmio_1 (
    .A_IN(addr_buffer_1_a_bus), .D_IN(pc_1_p11), .nMMIO_CS(nMMIO_CS), .nMEM_WR(nMEM_WR), .nMEM_RD(nMEM_RD),
    .KB_IN(keyboard_1_d), .KB_ST(keyboard_1_av), .D_OUT(pc_1_p11), .SPI_OUT(mmio_1_spi_out),
    .DISPLAY(mmio_1_display), .KB_EN(mmio_1_kb_en));
  STATUS_REG status_reg_1 (
    .D_IN(pc_1_p11), .Z_FLAG(alu_1_z_flag), .N_FLAG(alu_1_n_flag), .C_FLAG(alu_1_c_flag),
    .V_FLAG(alu_1_v_flag), .nFL_OE(nFL_OE), .nFLZN_LD(nFLZN_LD), .nFLCV_LD(nFLCV_LD), .FL_SEL(FL_SEL),
    .CLK(CLK_t), .nRST(nRST), .D_OUT(pc_1_p11), .Z(Z), .C(C), .N(N), .V(V));
  CTRLUNIT ctrlunit_1 (
    .OPC(opcode), .Z(Z), .C(C), .N(N), .V(V), .nMPC_RST(nMPC_RST), .nHALT(nHALT), .CLK(CLK_t), .nRST(nRST),
    .C0_15({ctrlunit_1_c0_15, nXYA_OE, XY_DIR, nXY_INC, nMPC_RST, nHBA_OE, nIRA_OE, nIRD_OE, nIRL_LD, nIRH_LD, nPCH_OE, nPCL_OE, PC_OE, nPC_LD, PC_INC}),
    .C16_31({nFL_OE, SHR_IN0, nSHR_OE, ALU_CIN, ALU_S2, ALU_S1, ALU_S0, A_SEL, nA_LD, nMAR_INC, nMAR_OE, nMARH_LD, nMARL_LD, MAR_DIR, REG_OE, REG_LD}),
    .C32_47({ctrlunit_1_c32_47, nJ_OE, nJ_LD, nHALT, SRC_SEL, nSPH_OE, nSPL_OE, nSP_OE, nSP_LD, SP_DIR, nSP_INC, FL_SEL, nFLCV_LD, nFLZN_LD}));
  Keyboard keyboard_1 (.C(mmio_1_kb_en), .en(1'b1), .D({keyboard_1_d_2, keyboard_1_d}), .av(keyboard_1_av));
  nMEM nmem_1 (
    .MEM_RD(ctrlunit_1_c0_15[14]), .MEM_WR(ctrlunit_1_c0_15[15]), .CLK(CLK_t), .nMEM_RD(nMEM_RD),
    .nMEM_WR(nMEM_WR));
  LED led_1 (.in(mmio_1_display[0]));
  LED led_2 (.in(mmio_1_display[1]));
  LED led_3 (.in(mmio_1_display[2]));
  LED led_4 (.in(mmio_1_display[3]));
  LED led_5 (.in(mmio_1_display[4]));
  LED led_6 (.in(mmio_1_display[5]));
  LED led_7 (.in(mmio_1_display[6]));
  LED led_8 (.in(mmio_1_display[7]));
  max7219_sim max7219_sim_1 (
    .SCLK(mmio_1_spi_out[0]), .MOSI(mmio_1_spi_out[1]), .CS(mmio_1_spi_out[4]), .DIG1(max7219_sim_1_dig1),
    .DIG2(max7219_sim_1_dig2), .DIG3(max7219_sim_1_dig3), .DIG4(max7219_sim_1_dig4),
    .DIG5(max7219_sim_1_dig5), .DIG6(max7219_sim_1_dig6), .DIG7(max7219_sim_1_dig7), .DIG8(max7219_sim_1_dig8));

  // Other names for the same wires on the sheet: Rdst[2:0] = opcode[2:0]

  // Notes on the sheet:
  //   clk_2: Hz: 25000
  //   contents of eeprom_1 (hex, n*v repeats v):
  //   6ba,7ff,f200,e9c0,e97d,602,700,8c0,e9c1,e923,e00,700,100,4820
  //   ,1400,4820,1400,4820,1400,4820,1400,4820,1400,4820,1400,4820,1400
  //   ,4820,1400,8e0,d000,dbc0,db0d,8c0,d016,dbc0,db07,2,3811,0,3812
  //   ,e9c0,e9a6,1,3842,e9c1,e923,3,3840,0,3841,2041,102,6020,e00,2040
  //   ,f00,189,7820,8c0,115,8020,d8c0,d87a,3000,d000,dbc0,db71,2040
  //   ,3811,2041,3812,e9c0,e9a6,2042,a800,3842,e9c1,e923,2041,102,6020
  //   ,e00,2040,f00,2040,6000,a00,2041,7000,b00,d8c0,d871,8e0,6040,f00
  //   ,8c0,7060,e00,d8c0,d871,8e0,189,7820,8c0,115,8020,d8c0,d871,1
  //   ,4800,e8c0,e85d,2040,6802,3840,2041,100,7020,3841,e8c0,e833,ff00
  //   ,e8c0,e87a,6bf,702,18,4800,10f,0,e9c1,e927,109,ff,e9c1,e927,10a
  //   ,8,e9c1,e927,10b,7,e9c1,e927,10c,1,e9c1,e927,ff,3831,3832,3833
  //   ,3834,3835,3836,3837,3838,0,3811,3812,3813,3814,e9c0,e9a9,f900
  //   ,0,3813,3814,100,298,396,480,508,e9c0,e9df,100,20f,342,440,507
  //   ,e9c0,e9df,100,201,386,4a0,506,e9c0,e9df,100,200,327,410,505,e9c0
  //   ,e9df,100,200,303,4e8,504,e9c0,e9df,100,200,300,464,503,e9c0,e9df
  //   ,100,200,300,40a,502,e9c0,e9df,2011,3821,e9c1,e90a,f900,3918,3a17
  //   ,3b16,3c15,3d1d,0,381c,2011,2115,7820,3819,2012,2116,8020,381a
  //   ,2013,2117,8020,381b,2014,2118,8020,d9c1,d903,3814,201b,3813,201a
  //   ,3812,2019,3811,201c,a800,381c,e8c0,e8e6,201d,6820,f00,600,201c
  //   ,4800,f900,8,381e,201e,6820,f00,600,3100,8e0,6810,f00,3000,c820
  //   ,dac1,da1d,4820,820,211e,e9c1,e927,201e,b000,381e,dbc1,db0c,f900
  //   ,6bf,703,4800,f900,3810,6bf,702,208,309,40a,50b,8,4800,820,e9c1
  //   ,e939,2010,e9c1,e939,18,4800,f900,6000,d8c1,d840,4840,4860,e8c1
  //   ,e842,4880,48a0,6000,d8c1,d849,4840,4860,e8c1,e84b,4880,48a0,6000
  //   ,d8c1,d852,4840,4860,e8c1,e854,4880,48a0,6000,d8c1,d85b,4840,4860
  //   ,e8c1,e85d,4880,48a0,6000,d8c1,d864,4840,4860,e8c1,e866,4880,48a0
  //   ,6000,d8c1,d86d,4840,4860,e8c1,e86f,4880,48a0,6000,d8c1,d876,4840
  //   ,4860,e8c1,e878,4880,48a0,6000,d8c1,d87e,4840,4860,f900,4880,48a0,f900
endmodule
