// Digital circuit CTRLUNIT.dig as structural Verilog
module CTRLUNIT (
  input  [7:0] OPC,
  input  Z,
  input  C,
  input  N,
  input  V,
  input  nMPC_RST,
  input  nHALT,
  input  CLK,
  input  nRST,
  output [15:0] C0_15,
  output [15:0] C16_31,
  output [15:0] C32_47
);

  wire _7408_1_pin3;
  wire [3:0] _74163_1_pin14;

  _7408 _7408_1 (
    .pin1(nRST), .pin2(nMPC_RST), .pin3(_7408_1_pin3), .pin4(1'b0), .pin5(1'b0), .pin7(1'b0), .pin9(1'b0),
    .pin10(1'b0), .pin12(1'b0), .pin13(1'b0), .pin14(1'b1));  // open: pin6, pin8, pin11
  _74163 _74163_1 (
    .pin1(_7408_1_pin3), .pin2(CLK), .pin3(1'b0), .pin4(1'b0), .pin5(1'b0), .pin6(1'b0), .pin7(nHALT),
    .pin8(1'b0), .pin9(1'b1), .pin10(nHALT), .pin11(_74163_1_pin14[3]), .pin12(_74163_1_pin14[2]),
    .pin13(_74163_1_pin14[1]), .pin14(_74163_1_pin14[0]), .pin16(1'b1));  // open: pin15
  ROM #(.AddrBits(16), .Bits(16)) _1ROM (.A({V, N, C, Z, _74163_1_pin14, OPC}), .sel(nRST), .D(C0_15));
  ROM #(.AddrBits(16), .Bits(16)) _2ROM (.A({V, N, C, Z, _74163_1_pin14, OPC}), .sel(nRST), .D(C16_31));
  ROM #(.AddrBits(16), .Bits(16)) _3ROM (.A({V, N, C, Z, _74163_1_pin14, OPC}), .sel(nRST), .D(C32_47));
  PullDown pulldown_1 (.out(C0_15[0]));
  PullUp pullup_1 (.out(C0_15[1]));
  PullDown pulldown_2 (.out(C16_31[0]));
  PullDown pulldown_3 (.out(C16_31[1]));
  PullUp pullup_2 (.out(C32_47[1]));
  PullUp pullup_3 (.out(C32_47[0]));
  PullDown pulldown_4 (.out(C0_15[2]));
  PullUp pullup_4 (.out(C0_15[3]));
  PullUp pullup_5 (.out(C0_15[4]));
  PullUp pullup_6 (.out(C0_15[5]));
  PullDown pulldown_5 (.out(C16_31[2]));
  PullUp pullup_7 (.out(C16_31[3]));
  PullUp pullup_8 (.out(C16_31[5]));
  PullUp pullup_9 (.out(C16_31[4]));
  PullDown pulldown_6 (.out(C32_47[2]));
  PullUp pullup_10 (.out(C32_47[3]));
  PullUp pullup_11 (.out(C32_47[5]));
  PullDown pulldown_7 (.out(C32_47[4]));
  PullUp pullup_12 (.out(C0_15[6]));
  PullUp pullup_13 (.out(C0_15[7]));
  PullUp pullup_14 (.out(C0_15[8]));
  PullUp pullup_15 (.out(C0_15[9]));
  PullDown pulldown_8 (.out(C16_31[8]));
  PullDown pulldown_9 (.out(C16_31[9]));
  PullUp pullup_16 (.out(C16_31[6]));
  PullUp pullup_17 (.out(C16_31[7]));
  PullDown pulldown_10 (.out(C32_47[9]));
  PullUp pullup_18 (.out(C32_47[6]));
  PullUp pullup_19 (.out(C32_47[8]));
  PullUp pullup_20 (.out(C32_47[7]));
  PullDown pulldown_11 (.out(C0_15[12]));
  PullUp pullup_21 (.out(C0_15[10]));
  PullUp pullup_22 (.out(C0_15[11]));
  PullUp pullup_23 (.out(C0_15[13]));
  PullDown pulldown_12 (.out(C16_31[10]));
  PullDown pulldown_13 (.out(C16_31[12]));
  PullUp pullup_24 (.out(C16_31[13]));
  PullDown pulldown_14 (.out(C16_31[11]));
  PullDown pulldown_15 (.out(C32_47[13]));
  PullUp pullup_25 (.out(C32_47[10]));
  PullUp pullup_26 (.out(C32_47[11]));
  PullUp pullup_27 (.out(C32_47[12]));
  PullDown pulldown_16 (.out(C0_15[14]));
  PullDown pulldown_17 (.out(C0_15[15]));
  PullUp pullup_28 (.out(C16_31[15]));
  PullDown pulldown_18 (.out(C16_31[14]));
  PullDown pulldown_19 (.out(C32_47[14]));
  PullDown pulldown_20 (.out(C32_47[15]));

  // Notes on the sheet:
  //   contents of _1ROM (hex, n*v repeats v):
  //   256*6f9a,8*2b7b,8*2bfb,2b7b,2b7b,2bfb,2bfb,23fb,33fb,83ff,abff
  //   ,8*2bfb,8*68ff,8*6bff,8*4bff,8*a8ff,8*abff,8*8bff,8*abff,8*2fff
  //   ,8*2bfb,8*2b7b,8*68ff,8*4bff,8*43ff,8*6bff,24*2bfb,16*2b7b,17*2bfb
  //   ,2fff,2bfb,2fff,2bfb,2fff,2bfb,2fff,2ffb,2f7b,2ffb,2f7b,2ffb,2f7b
  //   ,2ffb,2f7b,2ffb,2f7b,2ffb,2f7b,2ffb,2f7b,2ffb,2f7b,2bfb,bfd,2bfb
  //   ,bfd,2bfb,bfd,2bfb,bfd,2f7b,2f7b,2bfd,bfd,2ffb,2ffb,2bfb,2bfb
  //   ,2bff,2ffb,bff,5*2bfb,4fbf,2fff,4fbf,2bfb,2bfb,abff,2fff,2ffb
  //   ,88*2ffa,8*6bfe,105*2ffa,6ffe,2ffa,6ffe,2ffa,6ffe,2ffa,6ffe,2bfb
  //   ,6f9a,2bfb,6f9a,2bfb,6f9a,2bfb,6f9a,2bfb,6f9a,2bfb,6f9a,2bfb,6f9a
  //   ,2bfb,6f9a,8*2ffa,6f9a,6f9a,2ffa,2ffa,afee,afee,2ffa,2ffa,2ffa
  //   ,2bfa,6*2ffa,2b7a,6ffe,237a,2ffa,2ffa,2ffa,6bfe,202*2ffa,6ffe
  //   ,2ffa,6ffe,2ffa,6ffe,2ffa,6ffe,2ffa,2f7b,2ffa,2f7b,2ffa,2f7b,2ffa
  //   ,9*2f7b,8*2ffa,2f7a,2f7b,2ffa,2ffa,aff6,aff6,11*2ffa,6ffe,207*2ffa
  //   ,2bfc,2ffa,2bfc,2ffa,2bfc,2ffa,2bfc,2ffa,afee,2ffa,afee,2ffa,afee
  //   ,2ffa,afee,8*2bfc,8*2ffa,2bfc,afee,2ffa,2ffa,2bfc,bfc,11*2ffa
  //   ,2bfc,215*2ffa,aff6,2ffa,aff6,2ffa,aff6,2ffa,aff6,17*2ffa,aff6
  //   ,231*2ffa,2bfc,2ffa,2bfc,2ffa,2bfc,2ffa,2bfc,17*2ffa,2bfc,2326*2ffa
  //   ,256*6f9a,8*2b7b,8*2bfb,2b7b,2b7b,2bfb,2bfb,23fb,33fb,83ff,abff
  //   ,8*2bfb,8*68ff,8*6bff,8*4bff,8*a8ff,8*abff,8*8bff,8*abff,8*2fff
  //   ,8*2bfb,8*2b7b,8*68ff,8*4bff,8*43ff,8*6bff,24*2bfb,16*2b7b,17*2bfb
  //   ,2fff,2fff,2bfb,2bfb,2fff,2bfb,2fff,2ffb,2f7b,2f7b,2ffb,2ffb,2f7b
  //   ,2ffb,2f7b,2ffb,2f7b,2f7b,2ffb,2ffb,2f7b,2ffb,2f7b,2bfb,bfd,bfd
  //   ,2bfb,2bfb,bfd,2bfb,bfd,2f7b,2f7b,2bfd,bfd,2ffb,2ffb,2bfb,2bfb
  //   ,2bff,2ffb,bff,5*2bfb,4fbf,2fff,4fbf,2bfb,2bfb,abff,2fff,2ffb
  //   ,88*2ffa,8*6bfe,105*2ffa,6ffe,6ffe,2ffa,2ffa,6ffe,2ffa,6ffe,2bfb
  //   ,6f9a,6f9a,2bfb,2bfb,6f9a,2bfb,6f9a,2bfb,6f9a,6f9a,2bfb,2bfb,6f9a
  //   ,2bfb,6f9a,8*2ffa,6f9a,6f9a,2ffa,2ffa,afee,afee,2ffa,2ffa,2ffa
  //   ,2bfa,6*2ffa,2b7a,6ffe,237a,2ffa,2ffa,2ffa,6bfe,202*2ffa,6ffe,6ffe
  //   ,2ffa,2ffa,6ffe,2ffa,6ffe,2ffa,2f7b,2f7b,2ffa,2ffa,2f7b,2ffa,9*2f7b
  //   ,8*2ffa,2f7a,2f7b,2ffa,2ffa,aff6,aff6,11*2ffa,6ffe,207*2ffa,2bfc,2bfc
  //   ,2ffa,2ffa,2bfc,2ffa,2bfc,2ffa,afee,afee,2ffa,2ffa,afee,2ffa,afee
  //   ,8*2bfc,8*2ffa,2bfc,afee,2ffa,2ffa,2bfc,bfc,11*2ffa,2bfc,215*2ffa
  //   ,aff6,aff6,2ffa,2ffa,aff6,2ffa,aff6,17*2ffa,aff6,231*2ffa,2bfc,2bfc
  //   ,2ffa,2ffa,2bfc,2ffa,2bfc,17*2ffa,2bfc,2326*2ffa,256*6f9a,8*2b7b
  //   ,8*2bfb,2b7b,2b7b,2bfb,2bfb,23fb,33fb,83ff,abff,8*2bfb,8*68ff
  //   ,8*6bff,8*4bff,8*a8ff,8*abff,8*8bff,8*abff,8*2fff,8*2bfb,8*2b7b
  //   ,8*68ff,8*4bff,8*43ff,8*6bff,24*2bfb,16*2b7b,16*2bfb,2fff,2bfb,2bfb
  //   ,2fff,2bfb,2fff,2bfb,2fff,2f7b,2ffb,2ffb,2f7b,2ffb,2f7b,2ffb,2f7b,2f7b
  //   ,2ffb,2ffb,2f7b,2ffb,2f7b,2ffb,2f7b,bfd,2bfb,2bfb,bfd,2bfb,bfd
  //   ,2bfb,bfd,2f7b,2f7b,2bfd,bfd,2ffb,2ffb,2bfb,2bfb,2bff,2ffb,bff
  //   ,5*2bfb,4fbf,2fff,4fbf,2bfb,2bfb,abff,2fff,2ffb,88*2ffa,8*6bfe
  //   ,104*2ffa,6ffe,2ffa,2ffa,6ffe,2ffa,6ffe,2ffa,6ffe,6f9a,2bfb,2bfb
  //   ,6f9a,2bfb,6f9a,2bfb,6f9a,6f9a,2bfb,2bfb,6f9a,2bfb,6f9a,2bfb,6f9a
  //   ,8*2ffa,6f9a,6f9a,2ffa,2ffa,afee,afee,2ffa,2ffa,2ffa,2bfa,6*2ffa
  //   ,2b7a,6ffe,237a,2ffa,2ffa,2ffa,6bfe,201*2ffa,6ffe,2ffa,2ffa,6ffe
  //   ,2ffa,6ffe,2ffa,6ffe,2f7b,2ffa,2ffa,2f7b,2ffa,2f7b,2ffa,9*2f7b
  //   ,8*2ffa,2f7a,2f7b,2ffa,2ffa,aff6,aff6,11*2ffa,6ffe,206*2ffa,2bfc
  //   ,2ffa,2ffa,2bfc,2ffa,2bfc,2ffa,2bfc,afee,2ffa,2ffa,afee,2ffa,afee
  //   ,2ffa,afee,8*2bfc,8*2ffa,2bfc,afee,2ffa,2ffa,2bfc,bfc,11*2ffa
  //   ,2bfc,214*2ffa,aff6,2ffa,2ffa,aff6,2ffa,aff6,2ffa,aff6,17*2ffa
  //   ,aff6,230*2ffa,2bfc,2ffa,2ffa,2bfc,2ffa,2bfc,2ffa,2bfc,17*2ffa
  //   ,2bfc,2326*2ffa,256*6f9a,8*2b7b,8*2bfb,2b7b,2b7b,2bfb,2bfb,23fb
  //   ,33fb,83ff,abff,8*2bfb,8*68ff,8*6bff,8*4bff,8*a8ff,8*abff,8*8bff
  //   ,8*abff,8*2fff,8*2bfb,8*2b7b,8*68ff,8*4bff,8*43ff,8*6bff,24*2bfb
  //   ,16*2b7b,16*2bfb,2fff,2bfb,2fff,2bfb,2bfb,2fff,2bfb,2fff,2f7b
  //   ,2ffb,2f7b,2ffb,2ffb,2f7b,2ffb,2f7b,2f7b,2ffb,2f7b,2ffb,2ffb,2f7b
  //   ,2ffb,2f7b,bfd,2bfb,bfd,2bfb,2bfb,bfd,2bfb,bfd,2f7b,2f7b,2bfd
  //   ,bfd,2ffb,2ffb,2bfb,2bfb,2bff,2ffb,bff,5*2bfb,4fbf,2fff,4fbf,2bfb,2bfb
  //   ,abff,2fff,2ffb,88*2ffa,8*6bfe,104*2ffa,6ffe,2ffa,6ffe,2ffa,2ffa
  //   ,6ffe,2ffa,6ffe,6f9a,2bfb,6f9a,2bfb,2bfb,6f9a,2bfb,6f9a,6f9a,2bfb
  //   ,6f9a,2bfb,2bfb,6f9a,2bfb,6f9a,8*2ffa,6f9a,6f9a,2ffa,2ffa,afee,afee
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  //   contents of _2ROM (hex, n*v repeats v):
  //   256*a0f8,8*a0f9,8*a0fb,a0f0,a0e8,a0b8,a0bc,a0f8,a0f8,a0fa,a09a
  //   ,a0f2,a0ea,6*a0f8,8*a0f9,8*a0d9,8*a0f9,8*a0fa,8*a0da,16*a0fa,8*a0f8
  //   ,a77a,a77a,b57a,a57a,ad7a,ab7a,a97a,b4fa,a778,a778,b578,a578,ad78
  //   ,ab78,a978,b4f8,a778,a778,b578,a578,ad78,ab78,a978,b4f8,a778,a778
  //   ,b578,a578,ad78,ab78,a978,b4f8,8*a0f9,8*a099,24*a0f8,8*b7f9,8*a5f9
  //   ,16*80f9,9*a0f8,a0e8,a0f8,a0e8,a0f8,a0e8,a0f8,a0e8,a0f8,a0e8,a0f8
  //   ,a0e8,a0f8,a0e8,a0f8,a0e8,8*a0f8,a0e8,a0e8,a0d8,5*a0f8,a0d8,a0f0
  //   ,4*a0f8,a0f9,a0f9,5*a0f8,20f8,90*a0f8,8*a0f9,105*a0f8,a0f0,a0f8
  //   ,a0f0,a0f8,a0f0,a0f8,a0f0,33*a0f8,a0e8,6*a0f8,a0f9,a0f0,a078,206*a0f8
  //   ,a0e8,a0f8,a0e8,a0f8,a0e8,a0f8,a0e8,a0f8,a0f0,a0f8,a0f0,a0f8,a0f0
  //   ,a0f8,9*a0f0,8*a0f8,a0f0,a0f0,15*a0f8,a0e8,207*a0f8,a0d8,a0f8
  //   ,a0d8,a0f8,a0d8,a0f8,a0d8,8*a0f8,8*a0d8,8*a0f8,a0d8,a0f8,a0f8,a0f8
  //   ,a0d8,12*a0f8,a0d8,471*a0f8,a0d8,a0f8,a0d8,a0f8,a0d8,a0f8,a0d8
  //   ,17*a0f8,a0d8,2582*a0f8,8*a0f9,8*a0fb,a0f0,a0e8,a0b8,a0bc,a0f8,a0f8
  //   ,a0fa,a09a,a0f2,a0ea,6*a0f8,8*a0f9,8*a0d9,8*a0f9,8*a0fa,8*a0da
  //   ,16*a0fa,8*a0f8,a77a,a77a,b57a,a57a,ad7a,ab7a,a97a,b4fa,a778,a778
  //   ,b578,a578,ad78,ab78,a978,b4f8,a778,a778,b578,a578,ad78,ab78,a978
  //   ,b4f8,a778,a778,b578,a578,ad78,ab78,a978,b4f8,8*a0f9,8*a099,24*a0f8
  //   ,8*b7f9,8*a5f9,16*80f9,9*a0f8,a0e8,a0e8,a0f8,a0f8,a0e8,a0f8,a0e8
  //   ,a0f8,a0e8,a0e8,a0f8,a0f8,a0e8,a0f8,a0e8,8*a0f8,a0e8,a0e8,a0d8
  //   ,5*a0f8,a0d8,a0f0,4*a0f8,a0f9,a0f9,5*a0f8,20f8,90*a0f8,8*a0f9
  //   ,105*a0f8,a0f0,a0f0,a0f8,a0f8,a0f0,a0f8,a0f0,33*a0f8,a0e8,6*a0f8
  //   ,a0f9,a0f0,a078,206*a0f8,a0e8,a0e8,a0f8,a0f8,a0e8,a0f8,a0e8,a0f8
  //   ,a0f0,a0f0,a0f8,a0f8,a0f0,a0f8,9*a0f0,8*a0f8,a0f0,a0f0,15*a0f8
  //   ,a0e8,207*a0f8,a0d8,a0d8,a0f8,a0f8,a0d8,a0f8,a0d8,8*a0f8,8*a0d8
  //   ,8*a0f8,a0d8,a0f8,a0f8,a0f8,a0d8,12*a0f8,a0d8,471*a0f8,a0d8,a0d8
  //   ,a0f8,a0f8,a0d8,a0f8,a0d8,17*a0f8,a0d8,2582*a0f8,8*a0f9,8*a0fb
  //   ,a0f0,a0e8,a0b8,a0bc,a0f8,a0f8,a0fa,a09a,a0f2,a0ea,6*a0f8,8*a0f9
  //   ,8*a0d9,8*a0f9,8*a0fa,8*a0da,16*a0fa,8*a0f8,a77a,b77a,b57a,b57a
  //   ,ad7a,ab7a,a97a,b4fa,a778,b778,b578,b578,ad78,ab78,a978,b4f8,a778
  //   ,b778,b578,b578,ad78,ab78,a978,b4f8,a778,b778,b578,b578,ad78,ab78
  //   ,a978,b4f8,8*a0f9,8*a099,24*a0f8,8*b7f9,8*a5f9,8*80f9,8*c0f9,8*a0f8
  //   ,a0e8,a0f8,a0f8,a0e8,a0f8,a0e8,a0f8,a0e8,a0e8,a0f8,a0f8,a0e8,a0f8
  //   ,a0e8,a0f8,a0e8,8*a0f8,a0e8,a0e8,a0d8,5*a0f8,a0d8,a0f0,4*a0f8
  //   ,a0f9,a0f9,5*a0f8,20f8,90*a0f8,8*a0f9,104*a0f8,a0f0,a0f8,a0f8
  //   ,a0f0,a0f8,a0f0,a0f8,a0f0,33*a0f8,a0e8,6*a0f8,a0f9,a0f0,a078,205*a0f8
  //   ,a0e8,a0f8,a0f8,a0e8,a0f8,a0e8,a0f8,a0e8,a0f0,a0f8,a0f8,a0f0,a0f8
  //   ,a0f0,a0f8,9*a0f0,8*a0f8,a0f0,a0f0,15*a0f8,a0e8,206*a0f8,a0d8
  //   ,a0f8,a0f8,a0d8,a0f8,a0d8,a0f8,a0d8,8*a0f8,8*a0d8,8*a0f8,a0d8
  //   ,a0f8,a0f8,a0f8,a0d8,12*a0f8,a0d8,470*a0f8,a0d8,a0f8,a0f8,a0d8
  //   ,a0f8,a0d8,a0f8,a0d8,17*a0f8,a0d8,2582*a0f8,8*a0f9,8*a0fb,a0f0
  //   ,a0e8,a0b8,a0bc,a0f8,a0f8,a0fa,a09a,a0f2,a0ea,6*a0f8,8*a0f9,8*a0d9
  //   ,8*a0f9,8*a0fa,8*a0da,16*a0fa,8*a0f8,a77a,b77a,b57a,b57a,ad7a
  //   ,ab7a,a97a,b4fa,a778,b778,b578,b578,ad78,ab78,a978,b4f8,a778,b778
  //   ,b578,b578,ad78,ab78,a978,b4f8,a778,b778,b578,b578,ad78,ab78,a978
  //   ,b4f8,8*a0f9,8*a099,24*a0f8,8*b7f9,8*a5f9,8*80f9,8*c0f9,8*a0f8
  //   ,a0e8,a0f8,a0e8,a0f8,a0f8,a0e8,a0f8,a0e8,a0e8,a0f8,a0e8,a0f8,a0f8
  //   ,a0e8,a0f8,a0e8,8*a0f8,a0e8,a0e8,a0d8,5*a0f8,a0d8,a0f0,4*a0f8
  //   ,a0f9,a0f9,5*a0f8,20f8,90*a0f8,8*a0f9,104*a0f8,a0f0,a0f8,a0f0
  //   ,a0f8,a0f8,a0f0,a0f8,a0f0,33*a0f8,a0e8,6*a0f8,a0f9,a0f0,a078,205*a0f8
  //   ,a0e8,a0f8,a0e8,a0f8,a0f8,a0e8,a0f8,a0e8,a0f0,a0f8,a0f0,a0f8,a0f8
  //   ,a0f0,a0f8,9*a0f0,8*a0f8,a0f0,a0f0,15*a0f8,a0e8,206*a0f8,a0d8
  //   ,a0f8,a0d8,a0f8,a0f8,a0d8,a0f8,a0d8,8*a0f8,8*a0d8,8*a0f8,a0d8
  //   ,a0f8,a0f8,a0f8,a0d8,12*a0f8,a0d8,470*a0f8,a0d8,a0f8,a0d8,a0f8,a0f8
  //   ,a0d8,a0f8,a0d8,17*a0f8,a0d8,2582*a0f8,8*a0f9,8*a0fb,a0f0,a0e8
  //   ,a0b8,a0bc,a0f8,a0f8,a0fa,a09a,a0f2,a0ea,6*a0f8,8*a0f9,8*a0d9
  //   ,8*a0f9,8*a0fa,8*a0da,16*a0fa,8*a0f8,a77a,a77a,b57a,a57a,ad7a
  //   ,ab7a,a97a,b4fa,a778,a778,b578,a578,ad78,ab78,a978,b4f8,a778,a778
  //   ,b578,a578,ad78,ab78,a978,b4f8,a778,a778,b578,a578,ad78,ab78,a978
  //   ,b4f8,8*a0f9,8*a099,24*a0f8,8*b7f9,8*a5f9,16*80f9,9*a0f8,a0e8
  //   ,a0f8,a0e8,a0e8,a0f8,a0f8,a0e8,a0f8,a0e8,a0f8,a0e8,a0e8,a0f8,a0f8
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  //   contents of _3ROM (hex, n*v repeats v):
  //   312*1deb,8*1feb,16*1deb,8*1db3,8*1da3,4*1de8,1dea,1dea,1dea,5*1de8
  //   ,1dea,1dea,1dea,5*1de8,1dea,1dea,1dea,5*1de8,1dea,1dea,1dea,1de8
  //   ,40*1deb,16*1de8,16*1de9,1deb,1da3,1deb,1da3,1deb,1da3,1deb,1da3
  //   ,32*1deb,1dcb,1d6b,1dcb,1de3,1df3,1deb,1ceb,1d6b,1deb,1da3,1deb,1deb,1deb
  //   ,1db3,1da3,89*1deb,8*1dab,105*1deb,1da3,1deb,1da3,1deb,1da3,1deb
  //   ,1da3,28*1deb,1db3,1db3,1deb,1deb,1deb,1ceb,7*1deb,1da3,4*1deb
  //   ,1dac,19eb,201*1deb,1dab,1deb,1dab,1deb,1dab,1deb,1dab,28*1deb
  //   ,1db3,1db3,11*1deb,1dab,215*1deb,1db3,1deb,1db3,1deb,1db3,1deb
  //   ,1db3,17*1deb,1db3,231*1deb,1db3,1deb,1db3,1deb,1db3,1deb,1db3
  //   ,17*1deb,1db3,2894*1deb,8*1feb,16*1deb,8*1db3,8*1da3,4*1de8,1dea,1dea,1dea
  //   ,5*1de8,1dea,1dea,1dea,5*1de8,1dea,1dea,1dea,5*1de8,1dea,1dea,1dea
  //   ,1de8,40*1deb,16*1de8,16*1de9,1deb,1da3,1da3,1deb,1deb,1da3,1deb
  //   ,1da3,32*1deb,1dcb,1d6b,1dcb,1de3,1df3,1deb,1ceb,1d6b,1deb,1da3
  //   ,1deb,1deb,1deb,1db3,1da3,89*1deb,8*1dab,105*1deb,1da3,1da3,1deb,1deb
  //   ,1da3,1deb,1da3,28*1deb,1db3,1db3,1deb,1deb,1deb,1ceb,7*1deb,1da3
  //   ,4*1deb,1dac,19eb,201*1deb,1dab,1dab,1deb,1deb,1dab,1deb,1dab
  //   ,28*1deb,1db3,1db3,11*1deb,1dab,215*1deb,1db3,1db3,1deb,1deb,1db3
  //   ,1deb,1db3,17*1deb,1db3,231*1deb,1db3,1db3,1deb,1deb,1db3,1deb
  //   ,1db3,17*1deb,1db3,2894*1deb,8*1feb,16*1deb,8*1db3,8*1da3,4*1de8
  //   ,1dea,1dea,1dea,5*1de8,1dea,1dea,1dea,5*1de8,1dea,1dea,1dea,5*1de8
  //   ,1dea,1dea,1dea,1de8,40*1deb,16*1de8,16*1de9,1da3,1deb,1deb,1da3
  //   ,1deb,1da3,1deb,1da3,32*1deb,1dcb,1d6b,1dcb,1de3,1df3,1deb,1ceb
  //   ,1d6b,1deb,1da3,1deb,1deb,1deb,1db3,1da3,89*1deb,8*1dab,104*1deb
  //   ,1da3,1deb,1deb,1da3,1deb,1da3,1deb,1da3,28*1deb,1db3,1db3,1deb,1deb,1deb
  //   ,1ceb,7*1deb,1da3,4*1deb,1dac,19eb,200*1deb,1dab,1deb,1deb,1dab
  //   ,1deb,1dab,1deb,1dab,28*1deb,1db3,1db3,11*1deb,1dab,214*1deb,1db3
  //   ,1deb,1deb,1db3,1deb,1db3,1deb,1db3,17*1deb,1db3,230*1deb,1db3
  //   ,1deb,1deb,1db3,1deb,1db3,1deb,1db3,17*1deb,1db3,2894*1deb,8*1feb
  //   ,16*1deb,8*1db3,8*1da3,4*1de8,1dea,1dea,1dea,5*1de8,1dea,1dea,1dea
  //   ,5*1de8,1dea,1dea,1dea,5*1de8,1dea,1dea,1dea,1de8,40*1deb,16*1de8
  //   ,16*1de9,1da3,1deb,1da3,1deb,1deb,1da3,1deb,1da3,32*1deb,1dcb
  //   ,1d6b,1dcb,1de3,1df3,1deb,1ceb,1d6b,1deb,1da3,1deb,1deb,1deb,1db3
  //   ,1da3,89*1deb,8*1dab,104*1deb,1da3,1deb,1da3,1deb,1deb,1da3,1deb
  //   ,1da3,28*1deb,1db3,1db3,1deb,1deb,1deb,1ceb,7*1deb,1da3,4*1deb
  //   ,1dac,19eb,200*1deb,1dab,1deb,1dab,1deb,1deb,1dab,1deb,1dab,28*1deb
  //   ,1db3,1db3,11*1deb,1dab,214*1deb,1db3,1deb,1db3,1deb,1deb,1db3
  //   ,1deb,1db3,17*1deb,1db3,230*1deb,1db3,1deb,1db3,1deb,1deb,1db3
  //   ,1deb,1db3,17*1deb,1db3,2894*1deb,8*1feb,16*1deb,8*1db3,8*1da3
  //   ,4*1de8,1dea,1dea,1dea,5*1de8,1dea,1dea,1dea,5*1de8,1dea,1dea,1dea
  //   ,5*1de8,1dea,1dea,1dea,1de8,40*1deb,16*1de8,16*1de9,1deb,1da3
  //   ,1deb,1da3,1da3,1deb,1deb,1da3,32*1deb,1dcb,1d6b,1dcb,1de3,1df3
  //   ,1deb,1ceb,1d6b,1deb,1da3,1deb,1deb,1deb,1db3,1da3,89*1deb,8*1dab
  //   ,105*1deb,1da3,1deb,1da3,1da3,1deb,1deb,1da3,28*1deb,1db3,1db3
  //   ,1deb,1deb,1deb,1ceb,7*1deb,1da3,4*1deb,1dac,19eb,201*1deb,1dab
  //   ,1deb,1dab,1dab,1deb,1deb,1dab,28*1deb,1db3,1db3,11*1deb,1dab
  //   ,215*1deb,1db3,1deb,1db3,1db3,1deb,1deb,1db3,17*1deb,1db3,231*1deb
  //   ,1db3,1deb,1db3,1db3,1deb,1deb,1db3,17*1deb,1db3,2894*1deb,8*1feb
  //   ,16*1deb,8*1db3,8*1da3,4*1de8,1dea,1dea,1dea,5*1de8,1dea,1dea,1dea
  //   ,5*1de8,1dea,1dea,1dea,5*1de8,1dea,1dea,1dea,1de8,40*1deb,16*1de8
  //   ,16*1de9,1deb,1da3,1da3,1deb,1da3,1deb,1deb,1da3,32*1deb,1dcb
  //   ,1d6b,1dcb,1de3,1df3,1deb,1ceb,1d6b,1deb,1da3,1deb,1deb,1deb,1db3
  //   ,1da3,89*1deb,8*1dab,105*1deb,1da3,1da3,1deb,1da3,1deb,1deb,1da3
  //   ,28*1deb,1db3,1db3,1deb,1deb,1deb,1ceb,7*1deb,1da3,4*1deb,1dac
  //   ,19eb,201*1deb,1dab,1dab,1deb,1dab,1deb,1deb,1dab,28*1deb,1db3,1db3
  //   ,11*1deb,1dab,215*1deb,1db3,1db3,1deb,1db3,1deb,1deb,1db3,17*1deb
  //   ,1db3,231*1deb,1db3,1db3,1deb,1db3,1deb,1deb,1db3,17*1deb,1db3
  //   ,2894*1deb,8*1feb,16*1deb,8*1db3,8*1da3,4*1de8,1dea,1dea,1dea
  //   ,5*1de8,1dea,1dea,1dea,5*1de8,1dea,1dea,1dea,5*1de8,1dea,1dea,1dea
  //   ,1de8,40*1deb,16*1de8,16*1de9,1da3,1deb,1deb,1da3,1da3,1deb,1deb
  //   ,1da3,32*1deb,1dcb,1d6b,1dcb,1de3,1df3,1deb,1ceb,1d6b,1deb,1da3
  //   ,1deb,1deb,1deb,1db3,1da3,89*1deb,8*1dab,104*1deb,1da3,1deb,1deb
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endmodule
