// Digital circuit IR.dig as structural Verilog
module IR (
  input  [15:0] ROM_IN,
  input  nIRH_LD,
  input  nIRL_LD,
  input  nIRD_OE,
  input  nIRA_OE,
  input  CLK,
  output [4:0] _15_11,
  output [2:0] _10_8,
  output [2:0] _7_5,
  output [7:0] _0_7,
  output [7:0] AB
);

  wire _74377_2_pin2, _74377_2_pin5, _74377_2_pin6, _74377_2_pin9, _74377_2_pin12;

  _74377 _74377_1 (
    .pin1(nIRH_LD), .pin2(_10_8[0]), .pin3(ROM_IN[8]), .pin4(ROM_IN[9]), .pin5(_10_8[1]), .pin6(_10_8[2]),
    .pin7(ROM_IN[10]), .pin8(ROM_IN[11]), .pin9(_15_11[0]), .pin10(1'b0), .pin11(CLK), .pin12(_15_11[1]),
    .pin13(ROM_IN[12]), .pin14(ROM_IN[13]), .pin15(_15_11[2]), .pin16(_15_11[3]), .pin17(ROM_IN[14]),
    .pin18(ROM_IN[15]), .pin19(_15_11[4]), .pin20(1'b1));
  _74377 _74377_2 (
    .pin1(nIRL_LD), .pin2(_74377_2_pin2), .pin3(ROM_IN[0]), .pin4(ROM_IN[1]), .pin5(_74377_2_pin5),
    .pin6(_74377_2_pin6), .pin7(ROM_IN[2]), .pin8(ROM_IN[3]), .pin9(_74377_2_pin9), .pin10(1'b0),
    .pin11(CLK), .pin12(_74377_2_pin12), .pin13(ROM_IN[4]), .pin14(ROM_IN[5]), .pin15(_7_5[0]),
    .pin16(_7_5[1]), .pin17(ROM_IN[6]), .pin18(ROM_IN[7]), .pin19(_7_5[2]), .pin20(1'b1));
  // _74245 _74245_1: pin names not known; wires that end beside it: 1'b1, _74377_2_pin2, _74377_2_pin5, _74377_2_pin6, _74377_2_pin9, _74377_2_pin12, _7_5[0], _7_5[1], _7_5[2], 1'b0, 1'b1, 1'b1, nIRD_OE, _0_7[0], _0_7[1], _0_7[2], _0_7[3], _0_7[4], _0_7[5], _0_7[6], _0_7[7]
  _74245 _74245_2 (
    .pin1(1'b1), .pin2(_74377_2_pin2), .pin3(_74377_2_pin5), .pin4(_74377_2_pin6), .pin5(_74377_2_pin9),
    .pin6(_74377_2_pin12), .pin7(_7_5[0]), .pin8(_7_5[1]), .pin9(_7_5[2]), .pin10(1'b0), .pin11(AB[7]),
    .pin12(AB[6]), .pin13(AB[5]), .pin14(AB[4]), .pin15(AB[3]), .pin16(AB[2]), .pin17(AB[1]), .pin18(AB[0]),
    .pin19(nIRA_OE), .pin20(1'b1));

  // Other names for the same wires on the sheet: IRH_LD = nIRH_LD; IRL_LD = nIRL_LD
endmodule
