// Digital circuit J_REG.dig as structural Verilog
module J_REG (
  input  [7:0] D_BUS,
  input  nJ_LD,
  input  nJ_OE,
  input  CLK,
  output [7:0] AH_BUS
);

  wire _74574_1_pin11;

  _74574 _74574_1 (
    .pin1(nJ_OE), .pin2(D_BUS[0]), .pin3(D_BUS[1]), .pin4(D_BUS[2]), .pin5(D_BUS[3]), .pin6(D_BUS[4]),
    .pin7(D_BUS[5]), .pin8(D_BUS[6]), .pin9(D_BUS[7]), .pin10(1'b0), .pin11(_74574_1_pin11),
    .pin12(AH_BUS[7]), .pin13(AH_BUS[6]), .pin14(AH_BUS[5]), .pin15(AH_BUS[4]), .pin16(AH_BUS[3]),
    .pin17(AH_BUS[2]), .pin18(AH_BUS[1]), .pin19(AH_BUS[0]), .pin20(1'b1));
  _7432 _7432_1 (
    .pin1(nJ_LD), .pin2(CLK), .pin3(_74574_1_pin11), .pin4(1'b0), .pin5(1'b0), .pin7(1'b0), .pin9(1'b0),
    .pin10(1'b0), .pin12(1'b0), .pin13(1'b0), .pin14(1'b1));  // open: pin6, pin8, pin11
endmodule
