// Digital circuit PC.dig as structural Verilog
module PC (
  input  [15:0] A_IN,
  input  PC_INC,
  input  nPC_LD,
  input  PC_OE,
  input  nPCL_OE,
  input  nPCH_OE,
  input  CLK,
  input  RST,
  input  nRST,
  output [15:0] A_OUT,
  output [7:0] D_OUT
);

  wire _74161_1_pin11, _74161_1_pin12, _74161_1_pin13, _74161_1_pin14, _74161_1_pin15, _74161_2_pin11,
       _74161_2_pin12, _74161_2_pin13, _74161_2_pin14, _74161_2_pin15, _74161_3_pin11, _74161_3_pin12,
       _74161_3_pin13, _74161_3_pin14, _74161_3_pin15, _74161_4_pin11, _74161_4_pin12, _74161_4_pin13,
       _74161_4_pin14, nPC_LD_t, PC_OE_t;

  _7408 _7408_1 (
    .pin1(nRST), .pin2(nPC_LD), .pin3(nPC_LD_t), .pin4(1'b0), .pin5(1'b0), .pin7(1'b0), .pin9(1'b0),
    .pin10(1'b0), .pin12(1'b0), .pin13(1'b0), .pin14(1'b1));  // open: pin6, pin8, pin11
  _7432 _7432_1 (
    .pin1(RST), .pin2(PC_OE), .pin3(PC_OE_t), .pin4(1'b0), .pin5(1'b0), .pin7(1'b0), .pin9(1'b0),
    .pin10(1'b0), .pin12(1'b0), .pin13(1'b0), .pin14(1'b1));  // open: pin6, pin8, pin11
  _74161 _74161_1 (
    .pin1(1'b1), .pin2(CLK), .pin3(A_IN[0]), .pin4(A_IN[1]), .pin5(A_IN[2]), .pin6(A_IN[3]), .pin7(PC_INC),
    .pin8(1'b0), .pin9(nPC_LD_t), .pin10(PC_INC), .pin11(_74161_1_pin11), .pin12(_74161_1_pin12),
    .pin13(_74161_1_pin13), .pin14(_74161_1_pin14), .pin15(_74161_1_pin15), .pin16(1'b1));
  _74161 _74161_2 (
    .pin1(1'b1), .pin2(CLK), .pin3(A_IN[4]), .pin4(A_IN[5]), .pin5(A_IN[6]), .pin6(A_IN[7]), .pin7(PC_INC),
    .pin8(1'b0), .pin9(nPC_LD_t), .pin10(_74161_1_pin15), .pin11(_74161_2_pin11), .pin12(_74161_2_pin12),
    .pin13(_74161_2_pin13), .pin14(_74161_2_pin14), .pin15(_74161_2_pin15), .pin16(1'b1));
  _74161 _74161_3 (
    .pin1(1'b1), .pin2(CLK), .pin3(A_IN[8]), .pin4(A_IN[9]), .pin5(A_IN[10]), .pin6(A_IN[11]), .pin7(PC_INC),
    .pin8(1'b0), .pin9(nPC_LD_t), .pin10(_74161_2_pin15), .pin11(_74161_3_pin11), .pin12(_74161_3_pin12),
    .pin13(_74161_3_pin13), .pin14(_74161_3_pin14), .pin15(_74161_3_pin15), .pin16(1'b1));
  _74161 _74161_4 (
    .pin1(1'b1), .pin2(CLK), .pin3(A_IN[12]), .pin4(A_IN[13]), .pin5(A_IN[14]), .pin6(A_IN[15]),
    .pin7(PC_INC), .pin8(1'b0), .pin9(nPC_LD_t), .pin10(_74161_3_pin15), .pin11(_74161_4_pin11),
    .pin12(_74161_4_pin12), .pin13(_74161_4_pin13), .pin14(_74161_4_pin14), .pin16(1'b1));  // open: pin15
  _74245 _74245_1 (
    .pin1(1'b0), .pin2(D_OUT[0]), .pin3(D_OUT[1]), .pin4(D_OUT[2]), .pin5(D_OUT[3]), .pin6(D_OUT[4]),
    .pin7(D_OUT[5]), .pin8(D_OUT[6]), .pin9(D_OUT[7]), .pin10(1'b0), .pin11(_74161_2_pin11),
    .pin12(_74161_2_pin12), .pin13(_74161_2_pin13), .pin14(_74161_2_pin14), .pin15(_74161_1_pin11),
    .pin16(_74161_1_pin12), .pin17(_74161_1_pin13), .pin18(_74161_1_pin14), .pin19(nPCL_OE), .pin20(1'b1));
  _74245 _74245_2 (
    .pin1(1'b1), .pin2(_74161_1_pin14), .pin3(_74161_1_pin13), .pin4(_74161_1_pin12), .pin5(_74161_1_pin11),
    .pin6(_74161_2_pin14), .pin7(_74161_2_pin13), .pin8(_74161_2_pin12), .pin9(_74161_2_pin11), .pin10(1'b0),
    .pin11(A_OUT[7]), .pin12(A_OUT[6]), .pin13(A_OUT[5]), .pin14(A_OUT[4]), .pin15(A_OUT[3]),
    .pin16(A_OUT[2]), .pin17(A_OUT[1]), .pin18(A_OUT[0]), .pin19(PC_OE_t), .pin20(1'b1));
  _74245 _74245_3 (
    .pin1(1'b1), .pin2(_74161_3_pin14), .pin3(_74161_3_pin13), .pin4(_74161_3_pin12), .pin5(_74161_3_pin11),
    .pin6(_74161_4_pin14), .pin7(_74161_4_pin13), .pin8(_74161_4_pin12), .pin9(_74161_4_pin11), .pin10(1'b0),
    .pin11(A_OUT[15]), .pin12(A_OUT[14]), .pin13(A_OUT[13]), .pin14(A_OUT[12]), .pin15(A_OUT[11]),
    .pin16(A_OUT[10]), .pin17(A_OUT[9]), .pin18(A_OUT[8]), .pin19(PC_OE_t), .pin20(1'b1));
  _74245 _74245_4 (
    .pin1(1'b0), .pin2(D_OUT[0]), .pin3(D_OUT[1]), .pin4(D_OUT[2]), .pin5(D_OUT[3]), .pin6(D_OUT[4]),
    .pin7(D_OUT[5]), .pin8(D_OUT[6]), .pin9(D_OUT[7]), .pin10(1'b0), .pin11(_74161_4_pin11),
    .pin12(_74161_4_pin12), .pin13(_74161_4_pin13), .pin14(_74161_4_pin14), .pin15(_74161_3_pin11),
    .pin16(_74161_3_pin12), .pin17(_74161_3_pin13), .pin18(_74161_3_pin14), .pin19(nPCH_OE), .pin20(1'b1));
endmodule
