// Digital circuit RFILE.dig as structural Verilog
module RFILE (
  input  [7:0] DB_IN,
  input  [2:0] B_10_8,
  input  [2:0] B_7_5,
  input  REG_LD_EN,
  input  REG_OE_EN,
  input  nXY_INC,
  input  XY_DIR,
  input  nXYA_OE,
  input  SRC_SEL,
  input  CLK,
  input  RST,
  output [7:0] DB_OUT,
  output [15:0] AB_OUT,
  output A_LD,
  output A_OE
);

  wire _7404_1_pin2, _7404_1_pin4, _74157_1_pin4, _74157_1_pin7, _74157_1_pin9, B_LD, B_OE, C_LD, C_OE, D_LD,
       D_OE, E_LD, E_OE, F_LD, F_OE, pX_LD, pY_LD, RC0, RC1, RC2, X_LD, X_OE, XO0, XO1, XO2, XO3, XO4, XO5,
       XO6, XO7, Y_LD, Y_OE, YO0, YO1, YO2, YO3, YO4, YO5, YO6, YO7;

  _74245 _74245_1 (
    .pin1(1'b0), .pin2(DB_OUT[0]), .pin3(DB_OUT[1]), .pin4(DB_OUT[2]), .pin5(DB_OUT[3]), .pin6(DB_OUT[4]),
    .pin7(DB_OUT[5]), .pin8(DB_OUT[6]), .pin9(DB_OUT[7]), .pin10(1'b0), .pin11(XO7), .pin12(XO6),
    .pin13(XO5), .pin14(XO4), .pin15(XO3), .pin16(XO2), .pin17(XO1), .pin18(XO0), .pin19(X_OE), .pin20(1'b1));
  _74173 _74173_1 (
    .pin1(C_OE), .pin2(C_OE), .pin3(DB_OUT[0]), .pin4(DB_OUT[1]), .pin5(DB_OUT[2]), .pin6(DB_OUT[3]),
    .pin7(CLK), .pin8(1'b0), .pin9(C_LD), .pin10(C_LD), .pin11(DB_IN[3]), .pin12(DB_IN[2]), .pin13(DB_IN[1]),
    .pin14(DB_IN[0]), .pin15(RST), .pin16(1'b1));
  _74173 _74173_2 (
    .pin1(E_OE), .pin2(E_OE), .pin3(DB_OUT[0]), .pin4(DB_OUT[1]), .pin5(DB_OUT[2]), .pin6(DB_OUT[3]),
    .pin7(CLK), .pin8(1'b0), .pin9(E_LD), .pin10(E_LD), .pin11(DB_IN[3]), .pin12(DB_IN[2]), .pin13(DB_IN[1]),
    .pin14(DB_IN[0]), .pin15(RST), .pin16(1'b1));
  _74191 _74191_1 (
    .pin1(DB_IN[1]), .pin2(XO1), .pin3(XO0), .pin4(RC1), .pin5(XY_DIR), .pin6(XO2), .pin7(XO3), .pin8(1'b0),
    .pin9(DB_IN[3]), .pin10(DB_IN[2]), .pin11(X_LD), .pin13(RC2), .pin14(CLK), .pin15(DB_IN[0]), .pin16(1'b1));  // open: pin12
  _74173 _74173_3 (
    .pin1(C_OE), .pin2(C_OE), .pin3(DB_OUT[4]), .pin4(DB_OUT[5]), .pin5(DB_OUT[6]), .pin6(DB_OUT[7]),
    .pin7(CLK), .pin8(1'b0), .pin9(C_LD), .pin10(C_LD), .pin11(DB_IN[7]), .pin12(DB_IN[6]), .pin13(DB_IN[5]),
    .pin14(DB_IN[4]), .pin15(RST), .pin16(1'b1));
  _74173 _74173_4 (
    .pin1(E_OE), .pin2(E_OE), .pin3(DB_OUT[4]), .pin4(DB_OUT[5]), .pin5(DB_OUT[6]), .pin6(DB_OUT[7]),
    .pin7(CLK), .pin8(1'b0), .pin9(E_LD), .pin10(E_LD), .pin11(DB_IN[7]), .pin12(DB_IN[6]), .pin13(DB_IN[5]),
    .pin14(DB_IN[4]), .pin15(RST), .pin16(1'b1));
  _74191 _74191_2 (
    .pin1(DB_IN[5]), .pin2(XO5), .pin3(XO4), .pin4(RC2), .pin5(XY_DIR), .pin6(XO6), .pin7(XO7), .pin8(1'b0),
    .pin9(DB_IN[7]), .pin10(DB_IN[6]), .pin11(X_LD), .pin14(CLK), .pin15(DB_IN[4]), .pin16(1'b1));  // open: pin12, pin13
  _74245 _74245_2 (
    .pin1(1'b0), .pin2(AB_OUT[8]), .pin3(AB_OUT[9]), .pin4(AB_OUT[10]), .pin5(AB_OUT[11]), .pin6(AB_OUT[12]),
    .pin7(AB_OUT[13]), .pin8(AB_OUT[14]), .pin9(AB_OUT[15]), .pin10(1'b0), .pin11(XO7), .pin12(XO6),
    .pin13(XO5), .pin14(XO4), .pin15(XO3), .pin16(XO2), .pin17(XO1), .pin18(XO0), .pin19(nXYA_OE),
    .pin20(1'b1));
  _74173 _74173_5 (
    .pin1(B_OE), .pin2(B_OE), .pin3(DB_OUT[0]), .pin4(DB_OUT[1]), .pin5(DB_OUT[2]), .pin6(DB_OUT[3]),
    .pin7(CLK), .pin8(1'b0), .pin9(B_LD), .pin10(B_LD), .pin11(DB_IN[3]), .pin12(DB_IN[2]), .pin13(DB_IN[1]),
    .pin14(DB_IN[0]), .pin15(RST), .pin16(1'b1));
  _74173 _74173_6 (
    .pin1(D_OE), .pin2(D_OE), .pin3(DB_OUT[0]), .pin4(DB_OUT[1]), .pin5(DB_OUT[2]), .pin6(DB_OUT[3]),
    .pin7(CLK), .pin8(1'b0), .pin9(D_LD), .pin10(D_LD), .pin11(DB_IN[3]), .pin12(DB_IN[2]), .pin13(DB_IN[1]),
    .pin14(DB_IN[0]), .pin15(RST), .pin16(1'b1));
  _74173 _74173_7 (
    .pin1(F_OE), .pin2(F_OE), .pin3(DB_OUT[0]), .pin4(DB_OUT[1]), .pin5(DB_OUT[2]), .pin6(DB_OUT[3]),
    .pin7(CLK), .pin8(1'b0), .pin9(F_LD), .pin10(F_LD), .pin11(DB_IN[3]), .pin12(DB_IN[2]), .pin13(DB_IN[1]),
    .pin14(DB_IN[0]), .pin15(RST), .pin16(1'b1));
  _74191 _74191_3 (
    .pin1(DB_IN[1]), .pin2(YO1), .pin3(YO0), .pin4(nXY_INC), .pin5(XY_DIR), .pin6(YO2), .pin7(YO3),
    .pin8(1'b0), .pin9(DB_IN[3]), .pin10(DB_IN[2]), .pin11(Y_LD), .pin13(RC0), .pin14(CLK), .pin15(DB_IN[0]),
    .pin16(1'b1));  // open: pin12
  _74245 _74245_3 (
    .pin1(1'b0), .pin2(DB_OUT[0]), .pin3(DB_OUT[1]), .pin4(DB_OUT[2]), .pin5(DB_OUT[3]), .pin6(DB_OUT[4]),
    .pin7(DB_OUT[5]), .pin8(DB_OUT[6]), .pin9(DB_OUT[7]), .pin10(1'b0), .pin11(YO7), .pin12(YO6),
    .pin13(YO5), .pin14(YO4), .pin15(YO3), .pin16(YO2), .pin17(YO1), .pin18(YO0), .pin19(Y_OE), .pin20(1'b1));
  _74173 _74173_8 (
    .pin1(B_OE), .pin2(B_OE), .pin3(DB_OUT[4]), .pin4(DB_OUT[5]), .pin5(DB_OUT[6]), .pin6(DB_OUT[7]),
    .pin7(CLK), .pin8(1'b0), .pin9(B_LD), .pin10(B_LD), .pin11(DB_IN[7]), .pin12(DB_IN[6]), .pin13(DB_IN[5]),
    .pin14(DB_IN[4]), .pin15(RST), .pin16(1'b1));
  _74173 _74173_9 (
    .pin1(D_OE), .pin2(D_OE), .pin3(DB_OUT[4]), .pin4(DB_OUT[5]), .pin5(DB_OUT[6]), .pin6(DB_OUT[7]),
    .pin7(CLK), .pin8(1'b0), .pin9(D_LD), .pin10(D_LD), .pin11(DB_IN[7]), .pin12(DB_IN[6]), .pin13(DB_IN[5]),
    .pin14(DB_IN[4]), .pin15(RST), .pin16(1'b1));
  _74173 _74173_10 (
    .pin1(F_OE), .pin2(F_OE), .pin3(DB_OUT[4]), .pin4(DB_OUT[5]), .pin5(DB_OUT[6]), .pin6(DB_OUT[7]),
    .pin7(CLK), .pin8(1'b0), .pin9(F_LD), .pin10(F_LD), .pin11(DB_IN[7]), .pin12(DB_IN[6]), .pin13(DB_IN[5]),
    .pin14(DB_IN[4]), .pin15(RST), .pin16(1'b1));
  _74191 _74191_4 (
    .pin1(DB_IN[5]), .pin2(YO5), .pin3(YO4), .pin4(RC0), .pin5(XY_DIR), .pin6(YO6), .pin7(YO7), .pin8(1'b0),
    .pin9(DB_IN[7]), .pin10(DB_IN[6]), .pin11(Y_LD), .pin13(RC1), .pin14(CLK), .pin15(DB_IN[4]), .pin16(1'b1));  // open: pin12
  _74245 _74245_4 (
    .pin1(1'b0), .pin2(AB_OUT[0]), .pin3(AB_OUT[1]), .pin4(AB_OUT[2]), .pin5(AB_OUT[3]), .pin6(AB_OUT[4]),
    .pin7(AB_OUT[5]), .pin8(AB_OUT[6]), .pin9(AB_OUT[7]), .pin10(1'b0), .pin11(YO7), .pin12(YO6),
    .pin13(YO5), .pin14(YO4), .pin15(YO3), .pin16(YO2), .pin17(YO1), .pin18(YO0), .pin19(nXYA_OE),
    .pin20(1'b1));
  _7432 _7432_1 (
    .pin1(pX_LD), .pin2(CLK), .pin3(X_LD), .pin4(pY_LD), .pin5(CLK), .pin6(Y_LD), .pin7(1'b0), .pin9(1'b0),
    .pin10(1'b0), .pin12(1'b0), .pin13(1'b0), .pin14(1'b1));  // open: pin8, pin11
  _74157 _74157_1 (
    .pin1(SRC_SEL), .pin2(B_7_5[0]), .pin3(B_10_8[0]), .pin4(_74157_1_pin4), .pin5(B_7_5[1]),
    .pin6(B_10_8[1]), .pin7(_74157_1_pin7), .pin8(1'b0), .pin9(_74157_1_pin9), .pin10(B_10_8[2]),
    .pin11(B_7_5[2]), .pin13(1'b0), .pin14(1'b0), .pin15(1'b0), .pin16(1'b1));  // open: pin12
  _7404 _7404_1 (
    .pin1(REG_LD_EN), .pin2(_7404_1_pin2), .pin3(REG_OE_EN), .pin4(_7404_1_pin4), .pin5(1'b0), .pin7(1'b0),
    .pin9(1'b0), .pin11(1'b0), .pin13(1'b0), .pin14(1'b1));  // open: pin6, pin8, pin10, pin12
  _74138 _74138_1 (
    .pin1(B_10_8[0]), .pin2(B_10_8[1]), .pin3(B_10_8[2]), .pin4(_7404_1_pin2), .pin5(_7404_1_pin2),
    .pin6(REG_LD_EN), .pin7(pY_LD), .pin8(1'b0), .pin9(pX_LD), .pin10(F_LD), .pin11(E_LD), .pin12(D_LD),
    .pin13(C_LD), .pin14(B_LD), .pin15(A_LD), .pin16(1'b1));
  _74138 _74138_2 (
    .pin1(_74157_1_pin4), .pin2(_74157_1_pin7), .pin3(_74157_1_pin9), .pin4(_7404_1_pin4),
    .pin5(_7404_1_pin4), .pin6(REG_OE_EN), .pin7(Y_OE), .pin8(1'b0), .pin9(X_OE), .pin10(F_OE), .pin11(E_OE),
    .pin12(D_OE), .pin13(C_OE), .pin14(B_OE), .pin15(A_OE), .pin16(1'b1));

  // Other names for the same wires on the sheet: AO0 = AB_OUT[0]; AO1 = AB_OUT[1]; AO2 = AB_OUT[2]; AO3 = AB_OUT[3];
  //   AO4 = AB_OUT[4]; AO5 = AB_OUT[5]; AO6 = AB_OUT[6]; AO7 = AB_OUT[7]; AO8 = AB_OUT[8]; AO9 = AB_OUT[9];
  //   AO10 = AB_OUT[10]; AO11 = AB_OUT[11]; AO12 = AB_OUT[12]; AO13 = AB_OUT[13]; AO14 = AB_OUT[14];
  //   AO15 = AB_OUT[15]; D0 = DB_IN[0]; D1 = DB_IN[1]; D2 = DB_IN[2]; D3 = DB_IN[3]; D4 = DB_IN[4]; D5 = DB_IN[5];
  //   D6 = DB_IN[6]; D7 = DB_IN[7]; DO0 = DB_OUT[0]; DO1 = DB_OUT[1]; DO2 = DB_OUT[2]; DO3 = DB_OUT[3];
  //   DO4 = DB_OUT[4]; DO5 = DB_OUT[5]; DO6 = DB_OUT[6]; DO7 = DB_OUT[7]; XY_OE = nXYA_OE
endmodule
