// Digital circuit RST_HARDWARE.dig as structural Verilog
module RST_HARDWARE (
  input  CLK,
  input  RST_IN,
  output RST,
  output nRST
);

  wire _7474_1_pin5;

  _7474 _7474_1 (
    .pin1(nRST), .pin2(1'b0), .pin3(CLK), .pin4(RST_IN), .pin5(_7474_1_pin5), .pin7(1'b0), .pin8(nRST),
    .pin9(RST), .pin10(1'b1), .pin11(CLK), .pin12(_7474_1_pin5), .pin13(1'b1), .pin14(1'b1));  // open: pin6
endmodule
