// Digital circuit addr_buffer.dig as structural Verilog
module addr_buffer (
  input  [7:0] AB_L,
  input  nHBA_OE,
  input  nRST,
  output [15:0] A_BUS
);

  _74245 _74245_1 (
    .pin1(1'b1), .pin2(1'b0), .pin3(1'b0), .pin4(1'b0), .pin5(1'b0), .pin6(1'b0), .pin7(1'b0), .pin8(1'b0),
    .pin9(1'b0), .pin10(1'b0), .pin11(AB_L[7]), .pin12(AB_L[6]), .pin13(AB_L[5]), .pin14(AB_L[4]),
    .pin15(AB_L[3]), .pin16(AB_L[2]), .pin17(AB_L[1]), .pin18(AB_L[0]), .pin19(nRST), .pin20(1'b1));
  _74245 _74245_2 (
    .pin1(1'b1), .pin2(1'b0), .pin3(1'b0), .pin4(1'b0), .pin5(1'b0), .pin6(1'b0), .pin7(1'b0), .pin8(1'b1),
    .pin9(1'b1), .pin10(1'b0), .pin11(A_BUS[15]), .pin12(A_BUS[14]), .pin13(A_BUS[13]), .pin14(A_BUS[12]),
    .pin15(A_BUS[11]), .pin16(A_BUS[10]), .pin17(A_BUS[9]), .pin18(A_BUS[8]), .pin19(nRST), .pin20(1'b1));
  _74245 _74245_3 (
    .pin1(1'b1), .pin2(1'b0), .pin3(1'b0), .pin4(1'b0), .pin5(1'b0), .pin6(1'b0), .pin7(1'b0), .pin8(1'b0),
    .pin9(1'b0), .pin10(1'b0), .pin11(A_BUS[15]), .pin12(A_BUS[14]), .pin13(A_BUS[13]), .pin14(A_BUS[12]),
    .pin15(A_BUS[11]), .pin16(A_BUS[10]), .pin17(A_BUS[9]), .pin18(A_BUS[8]), .pin19(nHBA_OE), .pin20(1'b1));

  assign A_BUS[7:0] = AB_L;
endmodule
