// Digital circuit A(H)_BUFFER.dig as structural Verilog
module A_H__BUFFER (
  input  nHBA_OE,
  output [7:0] A_H__BUS
);

  _74245 _74245_1 (
    .pin1(1'b1), .pin2(1'b0), .pin3(1'b0), .pin4(1'b0), .pin5(1'b0), .pin6(1'b0), .pin7(1'b0), .pin8(1'b0),
    .pin9(1'b0), .pin10(1'b0), .pin11(A_H__BUS[7]), .pin12(A_H__BUS[6]), .pin13(A_H__BUS[5]),
    .pin14(A_H__BUS[4]), .pin15(A_H__BUS[3]), .pin16(A_H__BUS[2]), .pin17(A_H__BUS[1]), .pin18(A_H__BUS[0]),
    .pin19(nHBA_OE), .pin20(1'b1));
endmodule
