// Digital circuit INTERRUPTS.dig as structural Verilog
module INTERRUPTS (
  input  nSTOP,
  input  nTimer,
  input  nKB,
  input  I,
  input  nMPC_RST,
  input  nV_OE,
  input  VB0,
  input  nIRQ_CLR,
  input  CLK,
  output [15:0] AB,
  output IRQ_PEND
);

  wire _74148_1_pin6, _74148_1_pin7, _74148_1_pin9, _74148_1_pin15, and_1_out, and_2_out, and_3_out,
       not_1_out;

  _74148 _74148_1 (
    .pin1(1'b1), .pin2(nKB), .pin3(nTimer), .pin4(nSTOP), .pin5(1'b0), .pin6(_74148_1_pin6),
    .pin7(_74148_1_pin7), .pin8(1'b0), .pin9(_74148_1_pin9), .pin10(1'b1), .pin11(1'b1), .pin12(1'b1),
    .pin13(1'b1), .pin15(_74148_1_pin15), .pin16(1'b1));  // open: pin14
  not not_1 (not_1_out, CLK);
  and and_1 (and_1_out, not_1_out, _74148_1_pin15);
  and and_2 (and_2_out, I, nMPC_RST);
  and and_3 (and_3_out, and_1_out, and_2_out);
  _74245 _74245_1 (
    .pin1(1'b1), .pin2(VB0), .pin3(_74148_1_pin9), .pin4(_74148_1_pin7), .pin5(_74148_1_pin6), .pin6(1'b1),
    .pin7(1'b1), .pin8(1'b1), .pin9(1'b1), .pin10(1'b0), .pin11(AB[7]), .pin12(AB[6]), .pin13(AB[5]),
    .pin14(AB[4]), .pin15(AB[3]), .pin16(AB[2]), .pin17(AB[1]), .pin18(AB[0]), .pin19(nV_OE), .pin20(1'b1));
  _74245 _74245_2 (
    .pin1(1'b1), .pin2(1'b1), .pin3(1'b1), .pin4(1'b1), .pin5(1'b1), .pin6(1'b1), .pin7(1'b1), .pin8(1'b1),
    .pin9(1'b1), .pin10(1'b0), .pin11(AB[15]), .pin12(AB[14]), .pin13(AB[13]), .pin14(AB[12]),
    .pin15(AB[11]), .pin16(AB[10]), .pin17(AB[9]), .pin18(AB[8]), .pin19(nV_OE), .pin20(1'b1));
  _7474 _7474_1 (
    .pin1(nIRQ_CLR), .pin2(1'b1), .pin3(and_3_out), .pin4(1'b1), .pin5(IRQ_PEND), .pin7(1'b0), .pin10(1'b0),
    .pin11(1'b0), .pin12(1'b0), .pin13(1'b0), .pin14(1'b1));  // open: pin6, pin8, pin9
endmodule
