// Digital circuit INT_VECT.dig as structural Verilog
module INT_VECT (
  input  nV_OE,
  input  V_B0,
  output [15:0] AB
);

  _74245 _74245_1 (
    .pin1(1'b1), .pin2(V_B0), .pin3(1'b1), .pin4(1'b1), .pin5(1'b1), .pin6(1'b1), .pin7(1'b1), .pin8(1'b1),
    .pin9(1'b1), .pin10(1'b0), .pin11(AB[7]), .pin12(AB[6]), .pin13(AB[5]), .pin14(AB[4]), .pin15(AB[3]),
    .pin16(AB[2]), .pin17(AB[1]), .pin18(AB[0]), .pin19(nV_OE), .pin20(1'b1));
  _74245 _74245_2 (
    .pin1(1'b1), .pin2(1'b1), .pin3(1'b1), .pin4(1'b1), .pin5(1'b1), .pin6(1'b1), .pin7(1'b1), .pin8(1'b1),
    .pin9(1'b1), .pin10(1'b0), .pin11(AB[15]), .pin12(AB[14]), .pin13(AB[13]), .pin14(AB[12]),
    .pin15(AB[11]), .pin16(AB[10]), .pin17(AB[9]), .pin18(AB[8]), .pin19(nV_OE), .pin20(1'b1));
endmodule
