// Digital circuit IRQ_LATCH.dig as structural Verilog
module IRQ_LATCH (
  input  IRQ,
  input  I,
  input  nCLR_IRQ,
  input  nMPC_RST,
  output IRQ_PEND
);

  wire _7474_1_pin5, _7474_1_pin12;

  _7474 _7474_1 (
    .pin1(nCLR_IRQ), .pin2(1'b1), .pin3(IRQ), .pin4(1'b1), .pin5(_7474_1_pin5), .pin7(1'b0), .pin9(IRQ_PEND),
    .pin10(1'b1), .pin11(nMPC_RST), .pin12(_7474_1_pin12), .pin13(nCLR_IRQ), .pin14(1'b1));  // open: pin6, pin8
  _7408 _7408_1 (
    .pin1(_7474_1_pin5), .pin2(I), .pin3(_7474_1_pin12), .pin4(1'b0), .pin5(1'b0), .pin7(1'b0), .pin9(1'b0),
    .pin10(1'b0), .pin12(1'b0), .pin13(1'b0), .pin14(1'b1));  // open: pin6, pin8, pin11
endmodule
