// Digital circuit RST Buffer.dig as structural Verilog
module RST_Buffer (
  input  RST,
  output [15:0] A_BUS
);

  _74245 _74245_1 (
    .pin1(1'b1), .pin2(1'b0), .pin3(1'b0), .pin4(1'b0), .pin5(1'b0), .pin6(1'b0), .pin7(1'b0), .pin8(1'b0),
    .pin9(1'b0), .pin10(1'b0), .pin11(A_BUS[7]), .pin12(A_BUS[6]), .pin13(A_BUS[5]), .pin14(A_BUS[4]),
    .pin15(A_BUS[3]), .pin16(A_BUS[2]), .pin17(A_BUS[1]), .pin18(A_BUS[0]), .pin19(RST), .pin20(1'b1));
  _74245 _74245_2 (
    .pin1(1'b1), .pin2(1'b0), .pin3(1'b0), .pin4(1'b0), .pin5(1'b0), .pin6(1'b0), .pin7(1'b0), .pin8(1'b1),
    .pin9(1'b1), .pin10(1'b0), .pin11(A_BUS[15]), .pin12(A_BUS[14]), .pin13(A_BUS[13]), .pin14(A_BUS[12]),
    .pin15(A_BUS[11]), .pin16(A_BUS[10]), .pin17(A_BUS[9]), .pin18(A_BUS[8]), .pin19(RST), .pin20(1'b1));
endmodule
