// Digital circuit conection161to191.dig as structural Verilog
module conection161to191 (
);

  wire _74161_1_p3, _74161_1_p5, _74191_1_p1, _74191_1_p2;

  // _74191 _74191_1: pin names not known; wires that end beside it: _74191_1_p1, _74191_1_p2
  // _74161 _74161_1: pin names not known; wires that end beside it: _74191_1_p2, _74191_1_p1, _74161_1_p3, _74161_1_p3, _74161_1_p5, _74161_1_p5
endmodule
