// Digital circuit microPC.dig as structural Verilog
module microPC (
  input  CLK,
  input  nMPC_RST,
  output [3:0] microstep
);

  _74163 _74163_1 (
    .pin1(nMPC_RST), .pin2(CLK), .pin3(1'b0), .pin4(1'b0), .pin5(1'b0), .pin6(1'b0), .pin7(1'b1),
    .pin8(1'b0), .pin9(1'b1), .pin10(1'b1), .pin11(microstep[3]), .pin12(microstep[2]), .pin13(microstep[1]),
    .pin14(microstep[0]), .pin16(1'b1));  // open: pin15
endmodule
