// Digital circuit max7219_sim.dig as structural Verilog
module max7219_sim (
  input  SCLK,
  input  MOSI,
  input  CS,
  output [3:0] DIG1,
  output [3:0] DIG2,
  output [3:0] DIG3,
  output [3:0] DIG4,
  output [3:0] DIG5,
  output [3:0] DIG6,
  output [3:0] DIG7,
  output [3:0] DIG8
);

  wire decoder_1_out_1, decoder_1_out_2, decoder_1_out_3, decoder_1_out_4, decoder_1_out_5, decoder_1_out_6,
       decoder_1_out_7, decoder_1_out_8;
  wire [3:0] register_1_q, register_1_q_3;
  wire [15:5] register_1_q_2;
  wire [15:15] register_1_q_4;

  Register #(.Bits(16)) register_1 (
    .D({register_1_q_2[15:13], register_1_q_3, register_1_q_2[8:5], register_1_q, MOSI}), .C(SCLK),
    .en(1'b1),
    .Q({register_1_q_4[15], register_1_q_2[15:13], register_1_q_3, register_1_q_2[8:5], register_1_q}));
  Decoder #(.Selector_Bits(4)) decoder_1 (
    .sel(register_1_q_3), .out_1(decoder_1_out_1), .out_2(decoder_1_out_2), .out_3(decoder_1_out_3),
    .out_4(decoder_1_out_4), .out_5(decoder_1_out_5), .out_6(decoder_1_out_6), .out_7(decoder_1_out_7),
    .out_8(decoder_1_out_8));  // open: out_0, out_9, out_10, out_11, out_12, out_13, out_14, out_15
  Register #(.Bits(4)) register_2 (.D(register_1_q), .C(CS), .en(decoder_1_out_1), .Q(DIG1));
  Register #(.Bits(4)) register_3 (.D(register_1_q), .C(CS), .en(decoder_1_out_2), .Q(DIG2));
  Register #(.Bits(4)) register_4 (.D(register_1_q), .C(CS), .en(decoder_1_out_3), .Q(DIG3));
  Register #(.Bits(4)) register_5 (.D(register_1_q), .C(CS), .en(decoder_1_out_4), .Q(DIG4));
  Register #(.Bits(4)) register_6 (.D(register_1_q), .C(CS), .en(decoder_1_out_5), .Q(DIG5));
  Register #(.Bits(4)) register_7 (.D(register_1_q), .C(CS), .en(decoder_1_out_6), .Q(DIG6));
  Register #(.Bits(4)) register_8 (.D(register_1_q), .C(CS), .en(decoder_1_out_7), .Q(DIG7));
  Register #(.Bits(4)) register_9 (.D(register_1_q), .C(CS), .en(decoder_1_out_8), .Q(DIG8));
endmodule
