// Digital circuit nMEM.dig as structural Verilog
module nMEM (
  input  MEM_RD,
  input  MEM_WR,
  input  CLK,
  output nMEM_RD,
  output nMEM_WR
);

  wire _7400_1_pin3;

  _7400 _7400_1 (
    .pin1(CLK), .pin2(CLK), .pin3(_7400_1_pin3), .pin4(_7400_1_pin3), .pin5(MEM_RD), .pin6(nMEM_RD),
    .pin7(1'b0), .pin8(nMEM_WR), .pin9(_7400_1_pin3), .pin10(MEM_WR), .pin12(1'b0), .pin13(1'b0), .pin14(1'b1));  // open: pin11
endmodule
